// Logisim project char.circ as structural Verilog: 4 circuits, main circuit main
module main (
);

  wire and_1_out, and_2_out, and_3_out, and_4_out, and_5_out, and_6_out, and_7_out, button_1_out,
       button_2_out, button_3_out, Clear_out, Clock_out, n7483_1__14__cout, n7483_2__14__cout, not_1_out,
       not_2_out, not_3_out, or_1_out;
  wire [7:0] conditional_inverter_1_out, n7483_1__9__s1, program_counter_1_display, program_counter_1_out,
       program_counter_2_out, register_1_display, register_1_out, register_2_display, register_2_out,
       register_3_display, register_3_out, register_4_display, register_5_display, register_6_display,
       register_7_display, register_7_out, register_8_display, register_8_out;
  wire [15:1] rom_1_data;

  LED led_1 ();  // open: in
  LED led_2 ();  // open: in
  LED led_3 ();  // open: in
  Clock Clock (.out(Clock_out));
  Button Clear (.out(Clear_out));
  not not_1 (not_1_out, Clear_out);
  Button button_1 (.out(button_1_out));
  LED led_4 (.in(register_1_display[6]));
  LED led_5 (.in(register_1_display[7]));
  Program_Counter program_counter_1 (
    .OUT(program_counter_1_out), .CLOCK(Clock_out), .DISPLAY(program_counter_1_display), .IN(register_3_out),
    .SET(1'b1), .INC(button_1_out));
  LED led_6 (.in(program_counter_1_display[7]));
  LED led_7 (.in(register_1_display[4]));
  LED led_8 (.in(register_1_display[3]));
  LED led_9 (.in(register_1_display[2]));
  LED led_10 (.in(register_1_display[5]));
  Register register_1 (
    .READ(not_2_out), .IN(register_1_out), .WRITE(1'b0), .OUT(register_1_out), .DISPLAY(register_1_display),
    .Clock(Clock_out), .nCLEAR(not_1_out));
  Register register_2 (
    .READ(not_2_out), .IN(register_2_out), .WRITE(1'b0), .OUT(register_2_out), .DISPLAY(register_2_display),
    .Clock(Clock_out), .nCLEAR(not_1_out));
  LED led_11 (.in(register_3_out[7]));
  LED led_12 (.in(register_3_out[6]));
  LED led_13 (.in(program_counter_1_display[5]));
  LED led_14 (.in(program_counter_1_display[3]));
  LED led_15 (.in(program_counter_1_display[6]));
  LED led_16 (.in(program_counter_1_display[4]));
  LED led_17 (.in(register_1_display[1]));
  LED led_18 (.in(register_1_display[0]));
  LED led_19 (.in(register_3_out[5]));
  LED led_20 (.in(register_3_out[4]));
  LED led_21 (.in(register_3_out[3]));
  LED led_22 (.in(register_3_out[2]));
  Register register_3 (
    .READ(1'b1), .IN(register_3_out), .WRITE(1'b1), .OUT(register_3_out), .DISPLAY(register_3_display),
    .Clock(Clock_out), .nCLEAR(not_1_out));
  Register register_4 (
    .READ(1'b1), .IN(register_3_out), .WRITE(1'b1), .OUT(register_3_out), .DISPLAY(register_4_display),
    .Clock(Clock_out), .nCLEAR(not_1_out));
  Register register_5 (
    .READ(1'b1), .IN(register_3_out), .WRITE(1'b1), .OUT(register_3_out), .DISPLAY(register_5_display),
    .Clock(Clock_out), .nCLEAR(not_1_out));
  Register register_6 (
    .READ(1'b1), .IN(register_3_out), .WRITE(1'b1), .OUT(register_3_out), .DISPLAY(register_6_display),
    .Clock(Clock_out), .nCLEAR(not_1_out));
  LED led_23 (.in(program_counter_1_display[0]));
  LED led_24 (.in(program_counter_1_display[1]));
  LED led_25 (.in(program_counter_1_display[2]));
  LED led_26 (.in(register_2_display[5]));
  LED led_27 (.in(register_2_display[4]));
  LED led_28 (.in(register_2_display[7]));
  LED led_29 (.in(register_2_display[6]));
  LED led_30 (.in(register_3_out[0]));
  LED led_31 (.in(register_3_out[1]));
  LED led_32 (.in(register_3_display[6]));
  LED led_33 (.in(register_3_display[7]));
  LED led_34 (.in(register_3_display[5]));
  LED led_35 (.in(register_3_display[4]));
  LED led_36 (.in(register_4_display[7]));
  LED led_37 (.in(register_4_display[6]));
  LED led_38 (.in(register_4_display[5]));
  LED led_39 (.in(register_4_display[4]));
  LED led_40 (.in(register_5_display[6]));
  LED led_41 (.in(register_5_display[7]));
  LED led_42 (.in(register_5_display[5]));
  LED led_43 (.in(register_5_display[4]));
  LED led_44 (.in(register_6_display[5]));
  LED led_45 (.in(register_6_display[7]));
  LED led_46 (.in(register_6_display[4]));
  LED led_47 (.in(register_6_display[6]));
  LED led_48 (.in(register_2_display[3]));
  LED led_49 (.in(register_2_display[2]));
  LED led_50 (.in(register_2_display[0]));
  LED led_51 (.in(register_2_display[1]));
  LED led_52 (.in(register_3_display[2]));
  LED led_53 (.in(register_3_display[3]));
  LED led_54 (.in(register_3_display[0]));
  LED led_55 (.in(register_3_display[1]));
  LED led_56 (.in(register_4_display[0]));
  LED led_57 (.in(register_4_display[3]));
  LED led_58 (.in(register_4_display[2]));
  LED led_59 (.in(register_4_display[1]));
  LED led_60 (.in(register_5_display[0]));
  LED led_61 (.in(register_5_display[2]));
  LED led_62 (.in(register_5_display[3]));
  LED led_63 (.in(register_5_display[1]));
  LED led_64 (.in(register_6_display[2]));
  LED led_65 (.in(register_6_display[1]));
  LED led_66 (.in(register_6_display[0]));
  LED led_67 (.in(register_6_display[3]));
  Program_Counter program_counter_2 (
    .OUT(program_counter_2_out), .CLOCK(Clock_out), .INC(button_2_out));  // open: DISPLAY, IN, SET
  Button button_2 (.out(button_2_out));
  not not_2 (not_2_out, button_3_out);
  Button button_3 (.out(button_3_out));
  Conditional_Inverter conditional_inverter_1 (.IN(register_8_out), .Invert(1'b0), .OUT(conditional_inverter_1_out));
  and and_1 (and_1_out, 1'b1, ~rom_1_data[15]);  // AND_Gate
  Register register_7 (
    .READ(1'b1), .IN(register_3_out), .WRITE(1'b0), .OUT(register_7_out), .DISPLAY(register_7_display),
    .Clock(Clock_out), .nCLEAR(not_1_out));
  LED led_68 (.in(register_8_display[7]));
  Register register_8 (
    .READ(1'b1), .IN(register_3_out), .WRITE(1'b0), .OUT(register_8_out), .DISPLAY(register_8_display),
    .Clock(Clock_out), .nCLEAR(not_1_out));
  LED led_69 (.in(register_8_display[6]));
  and and_2 (and_2_out, and_1_out, ~rom_1_data[14]);  // AND_Gate
  LED led_70 (.in(register_7_display[4]));
  LED led_71 (.in(register_7_display[7]));
  LED led_72 (.in(register_7_display[6]));
  LED led_73 (.in(register_7_display[5]));
  _7483 u_7483_1 (
    ._1__A4(register_7_out[3]), ._2__S3(n7483_1__9__s1[2]), ._3__A3(register_7_out[2]),
    ._4__B3(conditional_inverter_1_out[3]), ._5__Vcc(1'b1), ._6__S2(n7483_1__9__s1[1]),
    ._7__B2(conditional_inverter_1_out[1]), ._8__A2(register_7_out[1]),
    ._16__B4(conditional_inverter_1_out[2]), ._15__S4(n7483_1__9__s1[3]), ._14__Cout(n7483_1__14__cout),
    ._13__Cin(1'b0), ._12__GND(1'b0), ._11__B1(conditional_inverter_1_out[0]), ._10__A1(register_7_out[0]),
    ._9__S1(n7483_1__9__s1[0]));
  LED led_74 (.in(register_8_display[3]));
  LED led_75 (.in(register_8_display[2]));
  LED led_76 (.in(register_8_display[4]));
  LED led_77 (.in(register_8_display[5]));
  LED led_78 (.in(rom_1_data[12]));
  LED led_79 (.in(rom_1_data[13]));
  LED led_80 (.in(rom_1_data[14]));
  LED led_81 (.in(rom_1_data[15]));
  LED led_82 (.in(register_7_display[3]));
  LED led_83 (.in(register_7_display[2]));
  LED led_84 (.in(register_7_display[0]));
  LED led_85 (.in(register_7_display[1]));
  LED led_86 (.in(register_8_display[0]));
  LED led_87 (.in(register_8_display[1]));
  LED led_88 (.in(rom_1_data[11]));
  ROM #(.dataWidth(16)) rom_1 (.addr(register_1_out), .data({rom_1_data, rom_1_data[1]}));  // open: sel
  _7483 u_7483_2 (
    ._1__A4(register_7_out[7]), ._2__S3(n7483_1__9__s1[6]), ._3__A3(register_7_out[6]),
    ._4__B3(conditional_inverter_1_out[6]), ._5__Vcc(1'b1), ._6__S2(n7483_1__9__s1[5]),
    ._7__B2(conditional_inverter_1_out[5]), ._8__A2(register_7_out[5]),
    ._16__B4(conditional_inverter_1_out[7]), ._15__S4(n7483_1__9__s1[7]), ._14__Cout(n7483_2__14__cout),
    ._13__Cin(n7483_1__14__cout), ._12__GND(1'b0), ._11__B1(conditional_inverter_1_out[4]),
    ._10__A1(register_7_out[4]), ._9__S1(n7483_1__9__s1[4]));
  LED led_89 (.in(rom_1_data[6]));
  LED led_90 (.in(rom_1_data[8]));
  LED led_91 (.in(rom_1_data[7]));
  LED led_92 (.in(rom_1_data[10]));
  LED led_93 (.in(rom_1_data[9]));
  and and_3 (and_3_out, 1'b1, rom_1_data[14]);
  and and_4 (and_4_out, and_3_out, ~rom_1_data[13]);  // AND_Gate
  LED led_94 (.in(n7483_2__14__cout));
  _27245 u_27245_1 (
    .DIR(1'b1), .A0(n7483_1__9__s1[0]), .A1(n7483_1__9__s1[1]), .A2(n7483_1__9__s1[2]),
    .A3(n7483_1__9__s1[3]), .A4(n7483_1__9__s1[4]), .A5(n7483_1__9__s1[5]), .A6(n7483_1__9__s1[6]),
    .A7(n7483_1__9__s1[7]), .B0(register_3_out[0]), .B1(register_3_out[1]), .B2(register_3_out[2]),
    .B3(register_3_out[3]), .B4(register_3_out[4]), .B5(register_3_out[5]), .B6(register_3_out[6]),
    .B7(register_3_out[7]), .ENABLE(not_3_out));
  or or_1 (or_1_out, 1'b0, 1'b0, 1'b0, 1'b0, 1'b0, 1'b0);
  not not_3 (not_3_out, or_1_out);
  LED led_95 (.in(rom_1_data[5]));
  LED led_96 (.in(rom_1_data[4]));
  LED led_97 (.in(rom_1_data[2]));
  LED led_98 (.in(rom_1_data[3]));
  and and_5 (and_5_out, and_3_out, rom_1_data[13]);
  and and_6 (and_6_out, and_4_out, ~rom_1_data[12]);  // AND_Gate
  LED led_99 (.in(rom_1_data[1]));
  and and_7 (and_7_out, and_6_out, rom_1_data[11]);
  // _27245 27245_2: pin names not known

  // Notes on the sheet:
  //   S
  //   O
  //   ?
  //   Power
  //   INSTRUCTION
  //   Data Bus
  //   OPERAND
  //   Instruction Bus
  //   Regiser: A
  //   Regiser: B
  //   Regiser: C
  //   Regiser: D
  //   CONTROL UNIT
  //   MEMORY CONTROL GOES HERE
  //   T1
  //   Register: mB
  //   contents of rom_1 (hex, n*v repeats v):
  //   0 800 14*0 1d0a 1d0b 1d0c 1d0d 1d0e 1d0f 10*0 3000 4800
  //   Register: mA
  //   T2
  //   T3
  //   Joseph A. Boyle
endmodule

module Register (
  input  READ,
  input  [7:0] IN,
  input  nCLEAR,
  input  Clock,
  input  WRITE,
  output [7:0] DISPLAY,
  output [7:0] OUT
);

  wire n27245_1_b0, n27245_1_b1, n27245_1_b2, n27245_1_b3, n27245_1_b4, n27245_1_b5, n27245_1_b6, n27245_1_b7;

  _27245 u_27245_1 (
    .DIR(1'b1), .A0(IN[0]), .A1(IN[1]), .A2(IN[2]), .A3(IN[3]), .A4(IN[4]), .A5(IN[5]), .A6(IN[6]),
    .A7(IN[7]), .B0(n27245_1_b0), .B1(n27245_1_b1), .B2(n27245_1_b2), .B3(n27245_1_b3), .B4(n27245_1_b4),
    .B5(n27245_1_b5), .B6(n27245_1_b6), .B7(n27245_1_b7), .ENABLE(READ));
  _27245 u_27245_2 (
    .DIR(1'b1), .A0(DISPLAY[0]), .A1(DISPLAY[1]), .A2(DISPLAY[2]), .A3(DISPLAY[3]), .A4(DISPLAY[4]),
    .A5(DISPLAY[5]), .A6(DISPLAY[6]), .A7(DISPLAY[7]), .B0(OUT[0]), .B1(OUT[1]), .B2(OUT[2]), .B3(OUT[3]),
    .B4(OUT[4]), .B5(OUT[5]), .B6(OUT[6]), .B7(OUT[7]), .ENABLE(WRITE));
  // _74273 74273_1: pin names not known; wires that end beside it: n27245_1_b0, n27245_1_b1, n27245_1_b2, n27245_1_b3, n27245_1_b4, n27245_1_b5, n27245_1_b6, n27245_1_b7, nCLEAR, Clock, DISPLAY[0], DISPLAY[1], DISPLAY[2], DISPLAY[3], DISPLAY[4], DISPLAY[5], DISPLAY[6], DISPLAY[7]
endmodule

module Program_Counter (
  input  [7:0] IN,
  input  SET,
  input  INC,
  input  CLOCK,
  output [7:0] OUT,
  output [7:0] DISPLAY
);

  wire and_1_out, n7483_1__2__s3, n7483_1__6__s2, n7483_1__9__s1, n7483_1__14__cout, n7483_1__15__s4,
       n7483_2__2__s3, n7483_2__6__s2, n7483_2__9__s1, n7483_2__15__s4, not_1_out, not_2_out, or_1_out;
  wire [7:0] n27245_1_b0;

  _27245 u_27245_1 (
    .DIR(1'b1), .A0(IN[0]), .A1(IN[1]), .A2(IN[2]), .A3(IN[3]), .A4(IN[4]), .A5(IN[5]), .A6(IN[6]),
    .A7(IN[7]), .B0(n27245_1_b0[0]), .B1(n27245_1_b0[1]), .B2(n27245_1_b0[2]), .B3(n27245_1_b0[3]),
    .B4(n27245_1_b0[4]), .B5(n27245_1_b0[5]), .B6(n27245_1_b0[6]), .B7(n27245_1_b0[7]), .ENABLE(SET));
  or or_1 (or_1_out, SET, not_2_out);
  not not_1 (not_1_out, or_1_out);
  Register register_1 (
    .READ(not_1_out), .IN(n27245_1_b0), .WRITE(1'b0), .OUT(OUT), .DISPLAY(DISPLAY), .Clock(CLOCK),
    .nCLEAR(1'b1));
  and and_1 (and_1_out, INC, SET);
  _7483 u_7483_1 (
    ._1__A4(OUT[3]), ._2__S3(n7483_1__2__s3), ._3__A3(OUT[2]), ._4__B3(1'b0), ._5__Vcc(1'b1),
    ._6__S2(n7483_1__6__s2), ._7__B2(1'b0), ._8__A2(OUT[1]), ._16__B4(1'b0), ._15__S4(n7483_1__15__s4),
    ._14__Cout(n7483_1__14__cout), ._13__Cin(1'b0), ._12__GND(1'b0), ._11__B1(1'b1), ._10__A1(OUT[0]),
    ._9__S1(n7483_1__9__s1));
  _7483 u_7483_2 (
    ._1__A4(OUT[7]), ._2__S3(n7483_2__2__s3), ._3__A3(OUT[6]), ._4__B3(1'b0), ._6__S2(n7483_2__6__s2),
    ._7__B2(1'b0), ._8__A2(OUT[5]), ._16__B4(1'b0), ._15__S4(n7483_2__15__s4), ._13__Cin(n7483_1__14__cout),
    ._11__B1(1'b0), ._10__A1(OUT[4]), ._9__S1(n7483_2__9__s1));  // open: _5__Vcc, _14__Cout, _12__GND
  not not_2 (not_2_out, and_1_out);
  _27245 u_27245_2 (
    .DIR(1'b1), .A0(n7483_1__9__s1), .A1(n7483_1__6__s2), .A2(n7483_1__2__s3), .A3(n7483_1__15__s4),
    .A4(n7483_2__9__s1), .A5(n7483_2__6__s2), .A6(n7483_2__2__s3), .A7(n7483_2__15__s4), .B0(n27245_1_b0[0]),
    .B1(n27245_1_b0[1]), .B2(n27245_1_b0[2]), .B3(n27245_1_b0[3]), .B4(n27245_1_b0[4]), .B5(n27245_1_b0[5]),
    .B6(n27245_1_b0[6]), .B7(n27245_1_b0[7]), .ENABLE(not_2_out));

  // Notes on the sheet:
  //   Program Register
endmodule

module Conditional_Inverter (
  input  [7:0] IN,
  input  Invert,
  output [7:0] OUT
);

  xor xor_1 (OUT[0], Invert, IN[0]);
  xor xor_2 (OUT[1], Invert, IN[1]);
  xor xor_3 (OUT[2], Invert, IN[2]);
  xor xor_4 (OUT[3], Invert, IN[3]);
  xor xor_5 (OUT[4], Invert, IN[4]);
  xor xor_6 (OUT[5], Invert, IN[5]);
  xor xor_7 (OUT[6], Invert, IN[6]);
  xor xor_8 (OUT[7], Invert, IN[7]);
endmodule
